# Fritzing sketch barndoor (saved by Fritzing 0.7.4b)
breadboards: 2

parts:
  C1 = Tantalum Capacitor [capacitance="1 μF" package="100 mil [THT, tantalum]"]
  C2 = Tantalum Capacitor [capacitance="1 μF" package="100 mil [THT, tantalum]"]
  J1 = female pin header, 2 pins [form="♀ (female)"]
  U1 = Voltage Regulator - 5V [package="TO220 [THT]"]
  J2 = female pin header, 2 pins [form="♀ (female)"]
  D1 = Rectifier Diode [part_number=1N4001 package="300 mil [THT]"]
  IC1 = L293D [package=THT]
  XTAL1 = CRYSTAL - kHz [frequency="16 Mhz"]
  U2 = atmega328 [package=dip]
  Power = Power plug
  R1 = Resistor [tolerance=±5% resistance=220 package=THT]
  LED1 = LED - 3mm [color="Green (570nm)" package="3 mm [THT]"]
  J3 = female pin header, 2 pins [form="♀ (female)"]
  J4 = female pin header, 1 pin [form="♀ (female)"]
  J5 = female pin header, 1 pin [form="♀ (female)"]
  J6 = female pin header, 3 pins [form="♀ (female)"]
  J7 = female pin header, 7 pins [form="♀ (female)"]
  J8 = female pin header, 6 pins [form="♀ (female)"]

nets:
  GND: C1.-, C2.-, U1.GND, IC1.0V, U2.GND#21, Power.GND, LED1.anode
  N1: C1.+, U1.output_voltage, IC1.Enable_1, IC1.Enable_2, IC1.+V, U2.VCC
  N2: C2.+, U1.input_voltage, D1.cathode, IC1.+Vmotor, R1.Pin_0
  N3: J1.pin1, IC1.Out_3_(_Controlled_by_Enable_2_)
  N4: J1.pin2, IC1.Out_4_(_Controlled_by_Enable_2_)
  N5: J2.pin1, IC1.Out_2_(_Controlled_by_Enable_1_)
  N6: J2.pin2, IC1.Out_1_(_Controlled_by_Enable_1_)
  N7: D1.anode, Power.VCC
  N8: IC1.In_1, U2.D3_(PWM)
  N9: IC1.In_2, U2.D2
  N10: IC1.In_3, U2.D6_(PWM)
  N11: IC1.In_4, U2.D5_(PWM)
  N12: XTAL1.pin_0, U2.XLAT2
  N13: XTAL1.pin_1, U2.XLAT1
  N14: U2.RESET, J6.pin3
  N15: U2.D0_(RX), J6.pin2
  N16: U2.D1_(TX), J6.pin1
  N17: U2.D4, J5.pin1
  N18: U2.GND#7, J4.pin1
  N19: U2.D7, J3.pin2
  N20: U2.D8, J3.pin1
  N21: U2.D9_(PWM), J7.pin1
  N22: U2.D10_(PWM), J7.pin2
  N23: U2.D11_(PWM), J7.pin3
  N24: U2.D12, J7.pin4
  N25: U2.D13, J7.pin5
  N26: U2.AVCC, J7.pin6
  N27: U2.AREF, J7.pin7
  N28: U2.A0, J8.pin1
  N29: U2.A1, J8.pin2
  N30: U2.A2, J8.pin3
  N31: U2.A3, J8.pin4
  N32: U2.A4, J8.pin5
  N33: U2.A5, J8.pin6
  N34: R1.Pin_1, LED1.cathode
